# Fritzing sketch Untitled+Sketch (saved by Fritzing 0.9.2b)
breadboards: 1

parts:
  부품1 = Arduino Mega ADK (Rev3)
  U1 = BUTTONPAD-4X4 [package=buttonpad-4x4]
  J1 = Basic Servo
  hc-sr1 = hc-sr04
  7_Segment1 = 7 Segment Display
  R1 = Resistor [tolerance=±5% resistance=220 package=THT]
  R2 = Resistor [tolerance=±5% resistance=220 package=THT]
  R3 = Resistor [tolerance=±5% resistance=220 package=THT]
  R4 = Resistor [tolerance=±5% resistance=220 package=THT]
  R5 = Resistor [tolerance=±5% resistance=220 package=THT]
  S1 = Pushbutton [package="[THT]"]
  S2 = Pushbutton [package="[THT]"]
  S4 = Pushbutton [package="[THT]"]
  S5 = Pushbutton [package="[THT]"]
  IC1 = ULN2003A [package="DIP16 [THT]"]
  M1 = Stepper Motor - Unipolar

nets:
  GND: 부품1.GND, J1.gnd, hc-sr1.GND, R1.Pin_0, R2.Pin_1, R3.Pin_0, R4.Pin_1, R5.Pin_1, IC1.0V
  N1: 부품1.D11_PWM, IC1.In_6
  N2: 부품1.D10_PWM, IC1.In_5
  N3: 부품1.D9_PWM, IC1.In_4
  N4: 부품1.D8_PWM, IC1.In_3
  VCC: 부품1.5V, J1.vcc, hc-sr1.VCC, S1.Pin_1, S1.Pin_2, S2.Pin_1, S2.Pin_2, S4.Pin_1, S4.Pin_2, S5.Pin_1, S5.Pin_2, IC1.In_7
  N5: 부품1.D2_PWM, R1.Pin_1, S1.Pin_3, S1.Pin_4
  N6: 부품1.D3_PWM, R4.Pin_0, S4.Pin_3, S4.Pin_4
  N7: 부품1.D4_PWM, R2.Pin_0, S5.Pin_3, S5.Pin_4
  N8: 부품1.D5_PWM, R5.Pin_0, S2.Pin_3, S2.Pin_4
  N9: 부품1.D6_PWM, J1.pulse
  N10: 부품1.D22, hc-sr1.Trig
  N11: 부품1.D23, hc-sr1.Echo
  N12: 부품1.D24, 7_Segment1.common_anode, R3.Pin_1
  N13: 부품1.D26, 7_Segment1.Segment_F
  N14: 부품1.D28, 7_Segment1.Segment_B
  N15: 부품1.D30, 7_Segment1.Segment_C
  N16: 부품1.D32, 7_Segment1.Segment_DP
  N17: 부품1.D34, 7_Segment1.Segment_E
  N18: 부품1.D36, 7_Segment1.Segment_D
  N19: 부품1.D39, U1.G$1_SIG2
  N20: 부품1.D41, U1.G$3_GND
  N21: 부품1.D43, U1.G$4_GRN
  N22: 부품1.D45, U1.G$4_BLU
  N23: 부품1.D47, U1.G$4_GND
  N24: 부품1.D49, U1.G$4_RED
  N25: 부품1.D51/MOSI, U1.G$2_SIG1
  N26: 부품1.D53/SS, U1.G$6_GRN
  N27: IC1.Out_6, M1.C
  N28: IC1.Out_5, M1.COMMON_2
  N29: IC1.Out_4, M1.B
  N30: IC1.Out_3, M1.D
  N31: IC1.Out_2, M1.COMMON_1
  N32: IC1.Out_1, M1.A
